// Logisim project Instruction_register1.circ as structural Verilog: 1 circuit, main circuit instruction_register1
module instruction_register1 (
  input  Alt,
  input  [7:0] D,
  input  clock,
  input  RI,
  input  RO,
  output [7:0] Q
);

  wire d_ff_1_q, d_ff_2_q, d_ff_3_q, d_ff_4_q, d_ff_5_q, d_ff_6_q, d_ff_7_q, d_ff_8_q, or_1_out;

  D_Flip_Flop d_ff_1 (.clk(clock), .D(D[0]), .Q(d_ff_1_q), .en(RI));  // open: Qn, preset, reset
  D_Flip_Flop d_ff_2 (.clk(clock), .D(D[1]), .Q(d_ff_2_q), .en(RI));  // open: Qn, preset, reset
  D_Flip_Flop d_ff_3 (.clk(clock), .D(D[2]), .Q(d_ff_3_q), .en(RI));  // open: Qn, preset, reset
  D_Flip_Flop d_ff_4 (.clk(clock), .D(D[3]), .Q(d_ff_4_q), .en(RI));  // open: Qn, preset, reset
  D_Flip_Flop d_ff_5 (.clk(clock), .D(D[4]), .Q(d_ff_5_q), .en(RI));  // open: Qn, preset, reset
  D_Flip_Flop d_ff_6 (.clk(clock), .D(D[5]), .Q(d_ff_6_q), .en(RI));  // open: Qn, preset, reset
  D_Flip_Flop d_ff_7 (.clk(clock), .D(D[6]), .Q(d_ff_7_q), .en(RI));  // open: Qn, preset, reset
  D_Flip_Flop d_ff_8 (.clk(clock), .D(D[7]), .Q(d_ff_8_q), .en(RI));  // open: Qn, preset, reset
  or or_1 (or_1_out, Alt, RO);
  assign Q[0] = or_1_out ? d_ff_1_q : 1'bz;  // Controlled_Buffer controlled_buffer_1
  assign Q[1] = or_1_out ? d_ff_2_q : 1'bz;  // Controlled_Buffer controlled_buffer_2
  assign Q[2] = or_1_out ? d_ff_3_q : 1'bz;  // Controlled_Buffer controlled_buffer_3
  assign Q[3] = or_1_out ? d_ff_4_q : 1'bz;  // Controlled_Buffer controlled_buffer_4
  assign Q[4] = RO ? d_ff_5_q : 1'bz;  // Controlled_Buffer controlled_buffer_5
  assign Q[5] = RO ? d_ff_6_q : 1'bz;  // Controlled_Buffer controlled_buffer_6
  assign Q[6] = RO ? d_ff_7_q : 1'bz;  // Controlled_Buffer controlled_buffer_7
  assign Q[7] = RO ? d_ff_8_q : 1'bz;  // Controlled_Buffer controlled_buffer_8
endmodule
