// Logisim project bit8_ALU0.circ as structural Verilog: 1 circuit, main circuit 8bit ALU
// e
module _8bit_ALU (
  input  [7:0] A,
  input  [7:0] B,
  input  [3:0] select,
  input  enabel,
  output [7:0] out
);

  wire [7:0] adder_1_out, divider_1_out, multiplier_1_out, subtractor_1_out;

  Adder adder_1 (.a(A), .b(B), .out(adder_1_out));  // open: cin, cout
  Subtractor subtractor_1 (.a(A), .b(B), .out(subtractor_1_out));  // open: bin, bout
  Multiplier multiplier_1 (.a(A), .b(B), .out(multiplier_1_out));  // open: cin, cout
  Divider divider_1 (.a(A), .b(B), .out(divider_1_out));  // open: upper, rem
  Multiplexer #(.select(4), .width(8)) multiplexer_1 (
    .in5(adder_1_out), .in6(subtractor_1_out), .in7(multiplier_1_out), .in8(divider_1_out), .out(out),
    .sel(select), .en(enabel));  // open: in0, in1, in2, in3, in4, in9, in10, in11, in12, in13, in14, in15
endmodule
