// Logisim project MARK 5.circ as structural Verilog: 1 circuit, main circuit bit8_computer5
module bit8_computer5 (
);

  wire and_1_out, and_2_out, clock_1_out, clock_2_out, clock_4_out, clock_5_out, controlled_buffer_6_out,
       counter_1_q, counter_5_q, n8bit_register_1_p2, n8bit_register_2_p2, n8bit_register_5_p2, not_1_out,
       not_2_out, not_3_out, not_4_out, not_5_out;
  wire [3:0] adder_1_out, bit_4register_1_p6, controlled_buffer_2_out, counter_2_q, counter_3_q, counter_4_q,
       n8bit_register_1_p1_2, pull_resistor_1_node, pull_resistor_2_node, register_1_q;
  wire [7:0] controlled_buffer_9_out, n8bit_register_2_p5, n8bit_register_3_p5, n8bit_register_4_p1,
       n8bit_register_4_p5, n8bit_register_5_p5, ram_1_data;
  wire [7:4] n8bit_register_1_p1;
  wire [19:0] pull_resistor_3_node;

  not not_1 (not_1_out, pull_resistor_3_node[15]);
  Pull_Resistor pull_resistor_1 (.node(pull_resistor_1_node));
  not not_2 (not_2_out, pull_resistor_3_node[15]);
  not not_3 (not_3_out, pull_resistor_3_node[12]);
  Clock clock_1 (.out(clock_1_out));
  Clock clock_2 (.out(clock_2_out));
  and and_1 (and_1_out, not_2_out, not_3_out);
  Counter #(.width(1), .max('h1)) counter_1 (.Q(counter_1_q), .clk(clock_1_out));  // open: load, D, count, carry, clr
  Counter #(.width(4), .max('hf)) counter_2 (
    .count(pull_resistor_3_node[15]), .Q(counter_2_q), .clk(clock_2_out));  // open: load, D, carry, clr
  assign pull_resistor_1_node = and_2_out ? pull_resistor_2_node : 4'bz;  // Controlled_Buffer controlled_buffer_1
  and and_2 (and_2_out, not_1_out, not_4_out);
  Register #(.width(4)) register_1 (.D(pull_resistor_1_node), .Q(register_1_q), .clk(counter_1_q));  // open: en, clr
  assign controlled_buffer_2_out = and_1_out ? register_1_q : 4'bz;  // Controlled_Buffer controlled_buffer_2
  assign controlled_buffer_2_out = pull_resistor_3_node[12] ? counter_3_q : 4'bz;  // Controlled_Buffer controlled_buffer_3
  Counter #(.width(4), .max('hf)) counter_3 (
    .count(pull_resistor_3_node[12]), .Q(counter_3_q), .clk(counter_1_q), .clr(pull_resistor_3_node[13]));  // open: load, D, carry
  // Probe on adder_1_out
  Adder #(.width(4)) adder_1 (.a(counter_2_q), .b(register_1_q), .out(adder_1_out));  // open: cin, cout
  assign controlled_buffer_2_out = pull_resistor_3_node[15] ? adder_1_out : 4'bz;  // Controlled_Buffer controlled_buffer_4
  Pull_Resistor pull_resistor_2 (.node(pull_resistor_2_node));
  // _8bit_Register 8bit_register_1: pin names not known; wires that end beside it: {n8bit_register_1_p1, n8bit_register_1_p1_2}, n8bit_register_1_p2, pull_resistor_3_node[18], pull_resistor_3_node[17], {n8bit_register_1_p1, n8bit_register_1_p1_2}
  // bit_4Register bit_4register_1: pin names not known; wires that end beside it: 1'b1, n8bit_register_1_p1_2, n8bit_register_1_p2, pull_resistor_3_node[2], 1'b1, bit_4register_1_p6
  Clock clock_3 (.out(n8bit_register_1_p2));
  Clock clock_4 (.out(clock_4_out));
  Clock clock_5 (.out(clock_5_out));
  Pull_Resistor pull_resistor_3 (.node(pull_resistor_3_node));
  ROM #(.addrWidth(4), .dataWidth(20)) rom_1 (
    .addr(controlled_buffer_2_out), .data(pull_resistor_3_node));  // open: sel
  RAM #(.addrWidth(4)) ram_1 (
    .addr(bit_4register_1_p6), .data(ram_1_data), .sel(1'b1), .clk(clock_4_out), .clr(1'b0));  // open: ld
  assign {n8bit_register_1_p1, n8bit_register_1_p1_2} = pull_resistor_3_node[3] ? ram_1_data : 8'bz;  // Controlled_Buffer controlled_buffer_5
  instruction_register1 instruction_register1_1 (
    .D({n8bit_register_1_p1, n8bit_register_1_p1_2}), .clock(clock_5_out),
    .Q({pull_resistor_2_node, n8bit_register_1_p1_2}), .Alt(pull_resistor_3_node[16]),
    .RI(pull_resistor_3_node[5]), .RO(pull_resistor_3_node[4]));
  not not_4 (not_4_out, pull_resistor_3_node[14]);
  // Probe on {n8bit_register_1_p1, n8bit_register_1_p1_2}
  not not_5 (not_5_out, n8bit_register_2_p2);
  assign controlled_buffer_6_out = not_4_out ? pull_resistor_3_node[0] : 1'bz;  // Controlled_Buffer controlled_buffer_6
  Counter #(.width(4), .max('hf)) counter_4 (
    .load(pull_resistor_3_node[16]), .D(n8bit_register_1_p1_2), .count(pull_resistor_3_node[1]),
    .Q(counter_4_q), .clk(counter_5_q));  // open: carry, clr
  Counter #(.width(1), .max('h1)) counter_5 (
    .Q(counter_5_q), .clk(n8bit_register_2_p2));  // open: load, D, count, carry, clr
  // Probe on n8bit_register_2_p5
  // _8bit_Register 8bit_register_2: pin names not known; wires that end beside it: {n8bit_register_1_p1, n8bit_register_1_p1_2}, n8bit_register_2_p2, pull_resistor_3_node[7], pull_resistor_3_node[6], n8bit_register_2_p5
  Clock clock_6 (.out(n8bit_register_2_p2));
  // _8bit_Register 8bit_register_3: pin names not known; wires that end beside it: {n8bit_register_1_p1, n8bit_register_1_p1_2}, n8bit_register_2_p2, pull_resistor_3_node[9], pull_resistor_3_node[8], n8bit_register_3_p5
  // Probe on n8bit_register_3_p5
  // _8bit_Register 8bit_register_4: pin names not known; wires that end beside it: n8bit_register_4_p1, not_5_out, 1'b1, pull_resistor_3_node[11], n8bit_register_4_p5
  // Probe on counter_4_q
  assign n8bit_register_1_p1_2 = controlled_buffer_6_out ? counter_4_q : 4'bz;  // Controlled_Buffer controlled_buffer_7
  _8bit_ALU u_8bit_alu_1 (
    .out(n8bit_register_4_p1), .A(n8bit_register_2_p5), .B(n8bit_register_3_p5),
    .enabel(pull_resistor_3_node[10]), .select(controlled_buffer_2_out));
  assign {n8bit_register_1_p1, n8bit_register_1_p1_2} = pull_resistor_3_node[11] ? n8bit_register_4_p5 : 8'bz;  // Controlled_Buffer controlled_buffer_8
  assign controlled_buffer_9_out = pull_resistor_3_node[11] ? n8bit_register_4_p5 : 8'bz;  // Controlled_Buffer controlled_buffer_9
  // Probe on n8bit_register_4_p1
  // _8bit_Register 8bit_register_5: pin names not known; wires that end beside it: controlled_buffer_9_out, n8bit_register_5_p2, 1'b1, 1'b1, n8bit_register_5_p5
  Clock clock_7 (.out(n8bit_register_5_p2));
  Hex_Digit_Display hex_digit_display_1 (.value(n8bit_register_5_p5[7:4]));  // open: dp
  Pull_Resistor pull_resistor_4 (.node(n8bit_register_5_p5));
  Hex_Digit_Display hex_digit_display_2 (.value(n8bit_register_5_p5[3:0]));  // open: dp

  // Notes on the sheet:
  //   clock attenuator
  //   incrementer
  //   h
  //   control logic
  //   sub counter
  //   Sel
  //   adder
  //   r
  //   CONTROL LOGIC
  //   REG C
  //   CO
  //   CI
  //   MAR
  //   MO
  //   MI
  //   RAM
  //   II
  //   contents of rom_1 (hex, n*v repeats v):
  //   1005 1028 1014 208a 220a 4*2542 12000 28004 808a 4200a 0 0 6800
  //   RO
  //   IR
  //   IO
  //   BUS
  //   CL
  //   CE
  //   REG A
  //   AI
  //   REG B
  //   BI
  //   clock attenuator
  //   AO
  //   mode
  //   BO
  //   REG D
  //   DO
  //   CO
  //   ALU
  //   EO
  //   DISPR
  //   RESULT(0x)
endmodule
